// Logisim project A2_GROUP-2.circ as structural Verilog: 4 circuits, main circuit main
module main (
  input  CS2,
  input  CS1,
  input  CS0,
  input  A3,
  input  B3,
  input  A2,
  input  B2,
  input  A1,
  input  B1,
  input  A0,
  input  B0,
  output Cout,
  output S3,
  output S2,
  output S1,
  output S0,
  output Z,
  output S,
  output C,
  output V
);

  wire _7432_2_out, _7432_out, modifiedadder_1_cprev, xi_yi_ckt_1_cin, xi_yi_ckt_1_x0, xi_yi_ckt_1_x1,
       xi_yi_ckt_1_x2, xi_yi_ckt_1_x3, xi_yi_ckt_1_y0, xi_yi_ckt_1_y1, xi_yi_ckt_1_y2, xi_yi_ckt_1_y3;

  Xi_Yi_Ckt xi_yi_ckt_1 (
    .CS2(CS2), .CS1(CS1), .CS0(CS0), .A0(A0), .B0(B0), .A1(A1), .B1(B1), .A2(A2), .B2(B2), .A3(A3), .B3(B3),
    .Cin(xi_yi_ckt_1_cin), .X3(xi_yi_ckt_1_x3), .X2(xi_yi_ckt_1_x2), .X1(xi_yi_ckt_1_x1),
    .X0(xi_yi_ckt_1_x0), .Y3(xi_yi_ckt_1_y3), .Y2(xi_yi_ckt_1_y2), .Y1(xi_yi_ckt_1_y1), .Y0(xi_yi_ckt_1_y0));
  modifiedAdder modifiedadder_1 (
    .X3(xi_yi_ckt_1_x3), .Cin(xi_yi_ckt_1_cin), .Y3(xi_yi_ckt_1_y3), .X2(xi_yi_ckt_1_x2),
    .Y2(xi_yi_ckt_1_y2), .X1(xi_yi_ckt_1_x1), .Y1(xi_yi_ckt_1_y1), .X0(xi_yi_ckt_1_x0), .Y0(xi_yi_ckt_1_y0),
    .S3(S), .S2(S2), .S1(S1), .S0(S0), .Cprev(modifiedadder_1_cprev), .Cout(C));
  or _7432 (_7432_out, S, S2);
  or _7432_2 (_7432_2_out, S1, S0);
  nor _7402 (Z, _7432_out, _7432_2_out);
  xor _7486_2 (V, modifiedadder_1_cprev, C);

  assign Cout = C;
  assign S3 = S;

  // Notes on the sheet:
  //   13
  //   12
  //   11
  //   8
  //   10
  //   8
  //   9
  //   10
  //   9
  //   10
  //   8
  //   9
endmodule

// Xi-Yi Ckt
module Xi_Yi_Ckt (
  input  CS2,
  input  CS1,
  input  CS0,
  input  A0,
  input  B0,
  input  A1,
  input  B1,
  input  A2,
  input  B2,
  input  A3,
  input  B3,
  output Cin,
  output X3,
  output X2,
  output X1,
  output X0,
  output Y3,
  output Y2,
  output Y1,
  output Y0
);

  wire and_1_out, and_2_out, and_3_out, and_4_out, and_5_out, and_6_out, and_7_out, and_8_out, nor_1_out,
       nor_2_out, not_1_out, not_2_out, not_3_out, not_4_out, not_5_out, not_6_out, or_1_out, or_2_out,
       xor_1_out, xor_2_out, xor_3_out, xor_4_out, xor_5_out, xor_6_out, xor_7_out;

  not not_1 (not_1_out, CS2);
  not not_2 (not_2_out, CS0);
  and and_1 (and_1_out, CS1, not_2_out);
  and and_2 (and_2_out, and_1_out, CS2);
  or or_1 (or_1_out, and_1_out, CS2);
  and and_3 (and_3_out, CS0, not_1_out);
  and and_4 (and_4_out, CS2, CS0);
  nor nor_1 (nor_1_out, and_2_out, and_3_out);
  not not_3 (not_3_out, A0);
  not not_4 (not_4_out, A1);
  not not_5 (not_5_out, A2);
  not not_6 (not_6_out, A3);
  xor xor_1 (xor_1_out, B2, 1'b1);
  nor nor_2 (nor_2_out, B1, B1);
  xor xor_2 (xor_2_out, B0, 1'b1);
  or or_2 (or_2_out, and_4_out, and_1_out);
  xor xor_3 (xor_3_out, B0, A0);
  and and_5 (and_5_out, A0, B0);
  xor xor_4 (xor_4_out, 1'b1, B3);
  nor nor_3 (Cin, nor_1_out, nor_1_out);
  and and_6 (and_6_out, B1, A1);
  xor xor_5 (xor_5_out, A1, B1);
  xor xor_6 (xor_6_out, A2, B2);
  and and_7 (and_7_out, A2, B2);
  xor xor_7 (xor_7_out, B3, A3);
  and and_8 (and_8_out, A3, B3);
  _74153 u_74153_1 (
    ._1__nG1(1'b0), ._2__B(CS2), ._3__1C3(not_4_out), ._4__1C2(xor_5_out), ._5__1C1(and_6_out), ._6__1C0(A1),
    ._7__Y1(X1), ._8__GND(1'b0), ._16__Vcc(1'b1), ._15__nG2(1'b0), ._14__A(or_2_out), ._13__2C3(not_3_out),
    ._12__2C2(xor_3_out), ._11__2C1(and_5_out), ._10__2C0(A0), ._9__Y2(X0));
  _74153 u_74153_2 (
    ._1__nG1(1'b0), ._2__B(CS2), ._3__1C3(not_6_out), ._4__1C2(xor_7_out), ._5__1C1(and_8_out), ._6__1C0(A3),
    ._7__Y1(X3), ._8__GND(1'b0), ._16__Vcc(1'b1), ._15__nG2(1'b0), ._14__A(or_2_out), ._13__2C3(not_5_out),
    ._12__2C2(xor_6_out), ._11__2C1(and_7_out), ._10__2C0(A2), ._9__Y2(X2));
  _74157 u_74157_1 (
    ._1__S(CS0), ._2__A1(B0), ._3__B1(xor_2_out), ._4__Y1(Y0), ._5__A2(B1), ._6__B2(nor_2_out), ._7__Y2(Y1),
    ._8__GND(1'b0), ._16__Vcc(1'b1), ._15__G(or_1_out), ._14__A4(B3), ._13__B4(xor_4_out), ._12__Y4(Y3),
    ._11__A3(B2), ._10__B3(xor_1_out), ._9__Y3(Y2));

  // Notes on the sheet:
  //   4
  //   12
  //   4
  //   3
  //   13
  //   1
  //   2
  //   5
  //   6
  //   10
  //   9
  //   8
  //   5
  //   6
  //   11
  //   3
  //   1
  //   2
  //   4
  //   5
  //   9
  //   11
  //   4
  //   5
  //   11
  //   12
  //   13
  //   12
  //   Cin
  //   2
  //   1
  //   3
  //   1
  //   2
  //   10
  //   9
  //   6
  //   10
  //   9
  //   8
  //   10
  //   12
  //   13
  //   1
  //   2
  //   B2'
  //   6
  //   B1'
  //   13
  //   B0'
  //   11
  //   5
  //   6
  //   3
  //   8
  //   8
  //   13
  //   12
  //   13
  //   12
  //   4
  //   5
  //   4
  //   5
  //   1
  //   2
  //   1
  //   2
  //   3
  //   B3'
  //   4
  //   11
  //   11
  //   6
  //   6
  //   3
  //   3
endmodule

// Adder
module modifiedAdder (
  input  X3,
  input  Cin,
  input  Y3,
  input  X2,
  input  Y2,
  input  X1,
  input  Y1,
  input  X0,
  input  Y0,
  output S3,
  output S2,
  output S1,
  output S0,
  output Cprev,
  output Cout
);

  _7483 u_7483_1 (
    ._1__A4(1'b0), ._2__S3(S2), ._3__A3(X2), ._4__B3(Y2), ._5__Vcc(1'b1), ._6__S2(S1), ._7__B2(Y1),
    ._8__A2(X1), ._16__B4(1'b0), ._15__S4(Cprev), ._13__Cin(Cin), ._12__GND(1'b0), ._11__B1(Y0),
    ._10__A1(X0), ._9__S1(S0));  // open: Cout
  _7483 u_7483_2 (
    ._1__A4(1'b0), ._3__A3(1'b0), ._4__B3(1'b0), ._5__Vcc(1'b1), ._6__S2(Cout), ._7__B2(1'b0), ._8__A2(1'b0),
    ._16__B4(1'b0), ._13__Cin(Cprev), ._12__GND(1'b0), ._11__B1(Y3), ._10__A1(X3), ._9__S1(S3));  // open: _2__S3, _15__S4, Cout

  // Notes on the sheet:
  //   1
  //   2
endmodule

module AllInOne (
  input  CS2,
  input  CS1,
  input  CS0,
  input  A3,
  input  A2,
  input  A1,
  input  A0,
  input  B3,
  input  B2,
  input  B1,
  input  B0,
  output Cin,
  output X3,
  output X2,
  output X1,
  output X0,
  output S3,
  output S2,
  output S1,
  output S0,
  output Y3,
  output Cprev,
  output Y2,
  output Y1,
  output Y0,
  output Z,
  output S,
  output Cout,
  output V
);

  wire n7402_1__1__1y, n7402_1__13__4y, n7404_1__2__1y, n7404_1__4__2y, n7404_1__8__4y, n7404_1__10__5y,
       n7404_1__12__6y, n7408_1__3__1y, n7408_1__6__2y, n7408_1__8__3y, n7408_1__11__4y, n7408_2__3__1y,
       n7408_2__6__2y, n7408_2__8__3y, n7408_2__11__4y, n7432_1__3__1y, n7432_1__6__2y, n7432_1__8__3y,
       n7432_1__11__4y, n7483_2__2__s3, n7486_1__3__1y, n7486_1__6__2y, n7486_1__8__3y, n7486_1__11__4y,
       n7486_2__3__1y, n7486_2__6__2y, n7486_2__11__4y;

  _7404 u_7404_1 (
    ._1__1A(CS0), ._2__1Y(n7404_1__2__1y), ._3__2A(CS2), ._4__2Y(n7404_1__4__2y), ._7__GND(1'b0),
    ._14__Vcc(1'b1), ._13__6A(A3), ._12__6Y(n7404_1__12__6y), ._11__5A(A2), ._10__5Y(n7404_1__10__5y),
    ._9__4A(A1), ._8__4Y(n7404_1__8__4y));  // open: _5__3A, _6__3Y
  _7408 u_7408_1 (
    ._1__1A(CS2), ._2__1B(CS0), ._3__1Y(n7408_1__3__1y), ._4__2A(CS1), ._5__2B(n7404_1__2__1y),
    ._6__2Y(n7408_1__6__2y), ._7__GND(1'b0), ._14__Vcc(1'b1), ._13__4B(n7404_1__4__2y), ._12__4A(CS0),
    ._11__4Y(n7408_1__11__4y), ._10__3B(CS2), ._9__3A(n7408_1__6__2y), ._8__3Y(n7408_1__8__3y));
  _7432 u_7432_1 (
    ._1__1A(n7408_1__3__1y), ._2__1B(n7408_1__6__2y), ._3__1Y(n7432_1__3__1y), ._4__2A(CS2),
    ._5__2B(n7408_1__6__2y), ._6__2Y(n7432_1__6__2y), ._7__GND(1'b0), ._14__Vcc(1'b1), ._13__4B(S),
    ._12__4A(S2), ._11__4Y(n7432_1__11__4y), ._10__3B(S1), ._9__3A(S0), ._8__3Y(n7432_1__8__3y));
  _7486 u_7486_1 (
    ._1__1A(B3), ._2__1B(A3), ._3__1Y(n7486_1__3__1y), ._4__2A(A2), ._5__2B(B2), ._6__2Y(n7486_1__6__2y),
    ._7__GND(1'b0), ._14__Vcc(1'b1), ._13__4B(B1), ._12__4A(A1), ._11__4Y(n7486_1__11__4y), ._10__3B(B0),
    ._9__3A(A0), ._8__3Y(n7486_1__8__3y));
  _7408 u_7408_2 (
    ._1__1A(A3), ._2__1B(B3), ._3__1Y(n7408_2__3__1y), ._4__2A(A2), ._5__2B(B2), ._6__2Y(n7408_2__6__2y),
    ._7__GND(1'b0), ._14__Vcc(1'b1), ._13__4B(B1), ._12__4A(A1), ._11__4Y(n7408_2__11__4y), ._10__3B(A0),
    ._9__3A(B0), ._8__3Y(n7408_2__8__3y));
  _7486 u_7486_2 (
    ._1__1A(1'b1), ._2__1B(B3), ._3__1Y(n7486_2__3__1y), ._4__2A(B2), ._5__2B(1'b1), ._6__2Y(n7486_2__6__2y),
    ._7__GND(1'b0), ._14__Vcc(1'b1), ._13__4B(B0), ._12__4A(1'b1), ._11__4Y(n7486_2__11__4y),
    ._10__3B(Cprev), ._9__3A(Cout), ._8__3Y(V));
  _74153 u_74153_1 (
    ._1__nG1(1'b0), ._2__B(CS2), ._3__1C3(n7404_1__8__4y), ._4__1C2(n7486_1__11__4y),
    ._5__1C1(n7408_2__11__4y), ._6__1C0(A1), ._7__Y1(X1), ._8__GND(1'b0), ._16__Vcc(1'b1), ._15__nG2(1'b0),
    ._14__A(n7432_1__3__1y), ._13__2C3(n7483_2__2__s3), ._12__2C2(n7486_1__8__3y), ._11__2C1(n7408_2__8__3y),
    ._10__2C0(A0), ._9__Y2(X0));
  _74153 u_74153_2 (
    ._1__nG1(1'b0), ._2__B(CS2), ._3__1C3(n7404_1__12__6y), ._4__1C2(n7486_1__3__1y),
    ._5__1C1(n7408_2__3__1y), ._6__1C0(A3), ._7__Y1(X3), ._8__GND(1'b0), ._16__Vcc(1'b1), ._15__nG2(1'b0),
    ._14__A(n7432_1__3__1y), ._13__2C3(n7404_1__10__5y), ._12__2C2(n7486_1__6__2y),
    ._11__2C1(n7408_2__6__2y), ._10__2C0(A2), ._9__Y2(X2));
  _74157 u_74157_1 (
    ._1__S(CS0), ._2__A1(B0), ._3__B1(n7486_2__11__4y), ._4__Y1(Y0), ._5__A2(B1), ._6__B2(n7402_1__13__4y),
    ._7__Y2(Y1), ._8__GND(1'b0), ._16__Vcc(1'b1), ._15__G(n7432_1__6__2y), ._14__A4(B3),
    ._13__B4(n7486_2__3__1y), ._12__Y4(Y3), ._11__A3(B2), ._10__B3(n7486_2__6__2y), ._9__Y3(Y2));
  _7402 u_7402_1 (
    ._1__1Y(n7402_1__1__1y), ._2__1A(n7408_1__8__3y), ._3__1B(n7408_1__11__4y), ._4__2Y(Cin),
    ._5__2A(n7402_1__1__1y), ._6__2B(n7402_1__1__1y), ._7__GND(1'b0), ._14__Vcc(1'b1),
    ._13__4Y(n7402_1__13__4y), ._12__4B(B1), ._11__4A(B1), ._10__3Y(Z), ._9__3B(n7432_1__8__3y),
    ._8__3A(n7432_1__11__4y));
  _7483 u_7483_1 (
    ._1__A4(1'b0), ._2__S3(S2), ._3__A3(X2), ._4__B3(Y2), ._5__Vcc(1'b1), ._6__S2(S1), ._7__B2(Y1),
    ._8__A2(X1), ._16__B4(1'b0), ._15__S4(Cprev), ._13__Cin(Cin), ._12__GND(1'b0), ._11__B1(Y0),
    ._10__A1(X0), ._9__S1(S0));  // open: Cout
  _7483 u_7483_2 (
    ._1__A4(1'b0), ._2__S3(n7483_2__2__s3), ._3__A3(A0), ._4__B3(1'b1), ._5__Vcc(1'b1), ._6__S2(Cout),
    ._7__B2(1'b0), ._8__A2(1'b0), ._16__B4(1'b0), ._13__Cin(Cprev), ._12__GND(1'b0), ._11__B1(Y3),
    ._10__A1(X3), ._9__S1(S));  // open: _15__S4, Cout

  assign S3 = S;
endmodule
