// Logisim project Floating_Point_Adder.circ as structural Verilog: 2 circuits, main circuit FPA
module FPA (
  input  [31:0] Input_2,
  input  [31:0] Input_1,
  output Denormalized_Input_1,
  output Denormalized_Input_2,
  output NaN_Input_1,
  output NaN_Input_2,
  output INF_Input_1,
  output INF_Input_2,
  output Overflow,
  output Underflow,
  output [31:0] Output,
  output Denormalized_Output,
  output NAN_Output,
  output INF_Output
);

  wire comparator_with_smaller_fraction_1_p5, comparator_with_smaller_fraction_1_p7, input_validator_1_p11,
       input_validator_1_p12, Manual_ALU_p6, multiplexer_1_out, multiplexer_2_out, n7486_1__3__1y,
       normalizer_1_overflow, normalizer_1_underflow, not_1_out;
  wire [4:0] comparator_with_smaller_fraction_1_p9;
  wire [8:0] comparator_with_smaller_fraction_1_p8;
  wire [9:0] shifter_2_out;
  wire [31:0] comparator_with_smaller_fraction_1_p6, normalizer_1_normalized_fraction, Rounder_p2,
       shifter_1_out;

  Multiplexer multiplexer_1 (
    .in0(Input_2[31]), .in1(Input_1[31]), .out(multiplexer_1_out),
    .sel(comparator_with_smaller_fraction_1_p7), .en(1'b1));
  Multiplexer multiplexer_2 (
    .in0(Input_1[31]), .in1(Input_2[31]), .out(multiplexer_2_out),
    .sel(comparator_with_smaller_fraction_1_p7), .en(1'b1));
  // Input_Validator input_validator_1: pin names not known; wires that end beside it: {2'b01, Input_1[21:0], {8{1'b0}}}, Input_1[30:22], {2'b01, Input_2[21:0], {8{1'b0}}}, Input_2[30:22], Denormalized_Input_1, Denormalized_Input_2, NaN_Input_1, NaN_Input_2, INF_Input_1, INF_Input_2, input_validator_1_p11, input_validator_1_p12
  // Comparator_With_Smaller_Fraction comparator_with_smaller_fraction_1: pin names not known; wires that end beside it: input_validator_1_p11, input_validator_1_p12, Input_1[30:22], Input_2[30:22], comparator_with_smaller_fraction_1_p5, comparator_with_smaller_fraction_1_p6, comparator_with_smaller_fraction_1_p7, comparator_with_smaller_fraction_1_p8, comparator_with_smaller_fraction_1_p9
  Shifter #(.width(32), .shift("lr")) shifter_1 (
    .in(comparator_with_smaller_fraction_1_p6), .\dist (comparator_with_smaller_fraction_1_p9),
    .out(shifter_1_out));
  // Manual_ALU Manual_ALU: pin names not known; wires that end beside it: comparator_with_smaller_fraction_1_p5, shifter_1_out, multiplexer_2_out, multiplexer_1_out, Output[31], Manual_ALU_p6
  Normalizer normalizer_1 (
    .Fraction(Rounder_p2), .Exponent(comparator_with_smaller_fraction_1_p8),
    .Normalized_Fraction(normalizer_1_normalized_fraction), .Normalized_Exponent(Output[30:22]),
    .Overflow(normalizer_1_overflow), .Underflow(normalizer_1_underflow));
  _7486 u_7486_1 (
    ._1__1A(normalizer_1_overflow), ._2__1B(normalizer_1_underflow), ._3__1Y(n7486_1__3__1y));  // open: _4__2A, _5__2B, _6__2Y, _7__GND, _14__Vcc, _13__4B, _12__4A, _11__4Y, _10__3B, _9__3A, _8__3Y
  _74157 u_74157_1 (
    ._1__S(n7486_1__3__1y), ._2__A1(normalizer_1_overflow), ._3__B1(normalizer_1_overflow),
    ._4__Y1(Overflow), ._15__G(1'b0));  // open: _5__A2, _6__B2, _7__Y2, _8__GND, _16__Vcc, _14__A4, _13__B4, _12__Y4, _11__A3, _10__B3, _9__Y3
  and and_1 (Underflow, normalizer_1_underflow, not_1_out);
  not not_1 (not_1_out, Denormalized_Output);
  // Rounder Rounder: pin names not known; wires that end beside it: Manual_ALU_p6, Rounder_p2
  Shifter #(.width(32)) shifter_2 (
    .in(normalizer_1_normalized_fraction), .\dist (5'b00010), .out({Output[21:0], shifter_2_out}));
  // Input_Validator input_validator_2: pin names not known; wires that end beside it: {Output[21:0], shifter_2_out}, Output[30:22], Denormalized_Output, NAN_Output, INF_Output

  // Notes on the sheet:
  //   (Sign bit taken to compare)
  //   Implicit bit(1)
  //   (Input 2 > Input 1)
  //   (Sign bit taken to compare)
  //   (sign bit of larger)
  //   (Sing bit of smaller)
  //   (Sum: might be denormalized)
  //   Implicit bit (1)
  //   (Sign of the result)
  //   (Might be again denormalized)
endmodule

module main (
  input  [31:0] Input_1,
  input  [31:0] Input_2,
  output Denormalized_Input_1,
  output Denormalized_Input_2,
  output [31:0] Output,
  output NAN_Input_1,
  output NAN_Input_2,
  output INF_Input_1,
  output INF_Input_2,
  output Overflow,
  output Underflow,
  output Denormalized_Output,
  output NAN_Output,
  output INF_Output
);

  FPA fpa_1 (
    .Input_2(Input_1), .Input_1(Input_2), .Denormalized_Input_1(Denormalized_Input_1),
    .Denormalized_Input_2(Denormalized_Input_2), .NaN_Input_1(NAN_Input_1), .NaN_Input_2(NAN_Input_2),
    .INF_Input_1(INF_Input_1), .INF_Input_2(INF_Input_2), .Overflow(Overflow), .Underflow(Underflow),
    .Output(Output), .Denormalized_Output(Denormalized_Output), .NAN_Output(NAN_Output),
    .INF_Output(INF_Output));
endmodule
