// Logisim project Normalizer.circ as structural Verilog: 2 circuits, main circuit main
module main (
);

  Normalizer normalizer_1 ();  // open: Fraction, Exponent, Normalized_Fraction, Normalized_Exponent, Overflow, Underflow
endmodule

module Normalizer (
  input  [31:0] Fraction,
  input  [8:0] Exponent,
  output [31:0] Normalized_Fraction,
  output [8:0] Normalized_Exponent,
  output Overflow,
  output Underflow
);

  wire alu_16_bit_1_p5, alu_16_bit_1_p6, mux_9_bit_1_p3, mux_9_bit_1_p4, n7408_1__3__1y;
  wire [0:0] comparator_9_bit_1_p3;
  wire [4:0] comparator_9_bit_1_p1, comparator_9_bit_1_p4;
  wire [15:0] alu_16_bit_1_p4;
  wire [31:0] shifter_1_out, shifter_2_out;

  // MUX_9_bit mux_9_bit_1: pin names not known; wires that end beside it: {9{1'b0}}, 9'h1e, mux_9_bit_1_p3, mux_9_bit_1_p4
  // Comparator_9_bit comparator_9_bit_1: pin names not known; wires that end beside it: {4'b0000, comparator_9_bit_1_p1}, mux_9_bit_1_p4, comparator_9_bit_1_p3[0], comparator_9_bit_1_p4
  // Priority_Encoder_32x5 priority_encoder_32x5_1: pin names not known; wires that end beside it: mux_9_bit_1_p3, comparator_9_bit_1_p1[4], comparator_9_bit_1_p1[3], Fraction, comparator_9_bit_1_p1[2], comparator_9_bit_1_p1[1], comparator_9_bit_1_p1[0]
  Shifter #(.width(32)) shifter_1 (.in(Fraction), .\dist (comparator_9_bit_1_p4), .out(shifter_1_out));
  Shifter #(.width(32), .shift("lr")) shifter_2 (.in(Fraction), .\dist (comparator_9_bit_1_p4), .out(shifter_2_out));
  // ALU_16_bit alu_16_bit_1: pin names not known; wires that end beside it: {{7{1'b0}}, Exponent}, {{11{1'b0}}, comparator_9_bit_1_p4}, {1'b1, comparator_9_bit_1_p3[0]}, alu_16_bit_1_p4, alu_16_bit_1_p5, alu_16_bit_1_p6
  // MUX_32_bit mux_32_bit_1: pin names not known; wires that end beside it: shifter_2_out, shifter_1_out, comparator_9_bit_1_p3[0], Normalized_Fraction
  _7408 u_7408_1 (
    ._1__1A(alu_16_bit_1_p5), ._2__1B(mux_9_bit_1_p3), ._3__1Y(n7408_1__3__1y), ._7__GND(1'b0),
    ._14__Vcc(1'b1));  // open: _4__2A, _5__2B, _6__2Y, _13__4B, _12__4A, _11__4Y, _10__3B, _9__3A, _8__3Y
  _7432 u_7432_1 (
    ._1__1A(alu_16_bit_1_p6), ._2__1B(n7408_1__3__1y), ._3__1Y(Underflow), ._7__GND(1'b0), ._14__Vcc(1'b1));  // open: _4__2A, _5__2B, _6__2Y, _13__4B, _12__4A, _11__4Y, _10__3B, _9__3A, _8__3Y
  // MUX_9_bit mux_9_bit_2: pin names not known; wires that end beside it: {9{1'b0}}, alu_16_bit_1_p4[8:0], mux_9_bit_1_p3, Normalized_Exponent
  // ALU_16_bit alu_16_bit_2: pin names not known; wires that end beside it: 16'h1fe, alu_16_bit_1_p4, 2'b11, Overflow

  // Notes on the sheet:
  //   (V)
  //   (To get Where the 1 is)
  //   (Whether LS or RS)
  //   (LS)
  //   (RS)
endmodule
